# Fritzing sketch Aquaduino (saved by Fritzing 0.7.7b)
breadboards: 2

parts:
  DS18S20 = IC, SIP package, 3 pins [chip_label=1820]
  U1 = Arduino Mega
  R1 = Resistor [tolerance=±5% resistance=10k package=THT]
  R2 = Resistor [tolerance=±5% resistance=10k package=THT]
  S1 = Reed switch [package=THT]
  Fuse1 = Fuse with Handler
  IC1 = IC, DIP package, 6 pins [chip_label=Relay]

nets (from the schematic view):
  N1: DS18S20.pin1, R1.Pin_1, S1.pin_2, Fuse1.Connector2
  N2: DS18S20.pin2, U1.D39, R1.Pin_0
  N3: DS18S20.pin3, U1.GND, R2.Pin_0, IC1.pin3
  N4: U1.+5V, Fuse1.Connector1, IC1.pin1
  N5: U1.D14, IC1.pin2
  N6: U1.D38, R2.Pin_1, S1.pin_1
